# Fritzing sketch RTII sketch (saved by Fritzing 0.9.2b)
breadboards: 1

parts:
  R1 = Resistor [tolerance=±5% resistance=220 package=THT]
  S1 = Tilt Switch [package=THT]
  S2 = Tilt Switch [package=THT]
  R2 = Resistor [tolerance=±5% resistance=220 package=THT]
  J1 = Basic Force Sensing Resistor (FSR) [package=THT]
  R3 = Resistor [tolerance=±5% resistance=220 package=THT]
  J2 = Infrared Proximity Sensor
  part = Arduino Uno (Rev3)

nets:
  N1: R1.Pin_0, S1.Pin_2, part.D5_PWM
  VCC: R1.Pin_1, R2.Pin_1, J1.pin_0, J2.Vcc, part.5V
  GND: S1.Pin_1, S2.Pin_1, R3.Pin_1, J2.GND, part.GND
  N2: S2.Pin_2, R2.Pin_0, part.D4
  N3: J1.pin_1, R3.Pin_0, part.A0
  N4: J2.Vout, part.A1
